// Logisim project LookAheadCarry.circ as structural Verilog: 2 circuits, main circuit main
module main (
  input  C0,
  input  [3:0] X,
  input  [3:0] Y,
  input  in_4
);

  wire and_1_out, and_2_out, and_3_out, and_4_out, and_5_out, and_6_out, and_7_out, and_8_out, and_9_out,
       and_10_out, and_11_out, and_12_out, and_13_out, and_14_out, or_1_out, or_2_out, or_3_out, xor_1_out,
       xor_2_out, xor_3_out, xor_4_out;
  wire [0:0] or_4_out;
  wire [3:0] S0_s;

  xor xor_1 (xor_1_out, X[0], Y[0]);
  and and_1 (and_1_out, X[0], Y[0]);
  xor xor_2 (xor_2_out, X[1], Y[1]);
  and and_2 (and_2_out, X[1], Y[1]);
  xor xor_3 (xor_3_out, X[2], Y[2]);
  and and_3 (and_3_out, X[2], Y[2]);
  xor xor_4 (xor_4_out, X[3], Y[3]);
  and and_4 (and_4_out, X[3], Y[3]);
  and and_5 (and_5_out, C0, xor_1_out);
  and and_6 (and_6_out, C0, xor_1_out, xor_2_out);
  and and_7 (and_7_out, and_1_out, xor_2_out);
  and and_8 (and_8_out, C0, xor_1_out, xor_2_out, xor_3_out);
  and and_9 (and_9_out, and_2_out, xor_3_out);
  and and_10 (and_10_out, xor_2_out, and_1_out, xor_3_out);
  and and_11 (and_11_out, C0, xor_2_out, xor_1_out, xor_3_out, xor_4_out);
  and and_12 (and_12_out, xor_4_out, and_1_out, xor_3_out, xor_4_out);
  and and_13 (and_13_out, and_3_out, xor_4_out);
  and and_14 (and_14_out, xor_4_out, xor_3_out, and_2_out);
  or or_1 (or_1_out, and_5_out, and_1_out);
  or or_2 (or_2_out, and_6_out, and_2_out, and_7_out);
  or or_3 (or_3_out, and_8_out, and_9_out, and_10_out, and_3_out);
  or or_4 (or_4_out[0], and_11_out, and_12_out, and_13_out, and_14_out, and_4_out);
  Hex_Digit_Display hex_digit_display_1 (.value(S0_s));  // open: dp
  Hex_Digit_Display hex_digit_display_2 (.value({{3{in_4}}, or_4_out[0]}));  // open: dp
  FullAdder S0 (.X(X[0]), .Y(Y[0]), .Cin(C0), .S(S0_s[0]));  // open: C
  FullAdder S1 (.X(X[1]), .Y(Y[1]), .Cin(or_1_out), .S(S0_s[1]));  // open: C
  FullAdder S2 (.X(X[2]), .Y(Y[2]), .Cin(or_2_out), .S(S0_s[2]));  // open: C
  FullAdder S3 (.X(X[3]), .Y(Y[3]), .Cin(or_3_out), .S(S0_s[3]));  // open: C

  // Notes on the sheet:
  //   P0
  //   G0
  //   P1
  //   G1
  //   P2
  //   G2
  //   P3
  //   G3
  //   C1
  //   C2
  //   C3
  //   C4
endmodule

module FullAdder (
  input  X,
  input  Y,
  input  Cin,
  output S,
  output C
);

  wire and_1_out, and_2_out, xor_1_out;

  xor xor_1 (xor_1_out, X, Y);
  and and_1 (and_1_out, X, Y);
  xor xor_2 (S, xor_1_out, Cin);
  and and_2 (and_2_out, xor_1_out, Cin);
  or or_1 (C, and_2_out, and_1_out);
endmodule
