// Logisim project UniversalShiftRegister.circ as structural Verilog: 1 circuit, main circuit main
module main (
  input  [3:0] in_1,
  input  D,
  input  [1:0] SelectLine,
  input  Set,
  input  Reset,
  output O3,
  output O0,
  output O1,
  output O2
);

  wire Clk_out, multiplexer_1_out, multiplexer_2_out, multiplexer_3_out, multiplexer_4_out;

  Clock Clk (.out(Clk_out));
  Multiplexer #(.select(2)) multiplexer_1 (
    .in0(D), .in1(O1), .in2(in_1[0]), .in3(O0), .out(multiplexer_1_out), .sel(SelectLine));
  D_Flip_Flop d_ff_1 (.D(multiplexer_1_out), .clk(Clk_out), .Q(O0), .preset(Set), .reset(Reset));  // open: Qn
  Multiplexer #(.select(2)) multiplexer_2 (
    .in0(O0), .in1(O2), .in2(in_1[1]), .in3(O1), .out(multiplexer_2_out), .sel(SelectLine));
  D_Flip_Flop d_ff_2 (.D(multiplexer_2_out), .clk(Clk_out), .Q(O1), .preset(Set), .reset(Reset));  // open: Qn
  Multiplexer #(.select(2)) multiplexer_3 (
    .in0(O1), .in1(O3), .in2(in_1[2]), .in3(O2), .out(multiplexer_3_out), .sel(SelectLine));
  D_Flip_Flop d_ff_3 (.D(multiplexer_3_out), .clk(Clk_out), .Q(O2), .preset(Set), .reset(Reset));  // open: Qn
  Multiplexer #(.select(2)) multiplexer_4 (
    .in0(O2), .in1(D), .in2(in_1[3]), .in3(O3), .out(multiplexer_4_out), .sel(SelectLine));
  D_Flip_Flop d_ff_4 (.D(multiplexer_4_out), .clk(Clk_out), .Q(O3), .preset(Set), .reset(Reset));  // open: Qn
endmodule
